# Fritzing sketch Dishwasher (saved by Fritzing 0.9.3b)

parts:
  WeMos_D1_Mini3 = WeMos D1 Mini
  Squix1 = OLED 0.96" 128x64 I2C SSD1306 (GND/VCC)
  IC6 = DIP - 4 pins [chip_label=L package="DIP (Dual Inline) [THT]"]
  U2 = 2-Channel 5v Relay Shield [package=relay-2ch5v10a]
  U3 = 2-Channel 5v Relay Shield [package=relay-2ch5v10a]
  DS1 = DS18B20 1-Wire Temperature Sensor [part_number=DS18B20]
  JP1 = Header 3 [package=screwterminal-3.5mm-3_lock.007s]
  M2 = DC Motor
  L1 = Solenoid  # not connected
  L2 = Solenoid  # not connected
  HLK-PM1 = HLK-PM01
  U4 = SWITCH_SPDT [package=kps-1290]
  M1 = DC Motor [part_number=DrainPump]  # not connected
  L3 = Solenoid  # not connected
  IC7 = DIP - 4 pins [chip_label=L package="DIP (Dual Inline) [THT]"]

nets:
  VCC: WeMos_D1_Mini3.3V3, Squix1.VCC, U2.VCC, U3.VCC, DS1.VDD
  N1: WeMos_D1_Mini3.5V, HLK-PM1.+Vo
  N2: WeMos_D1_Mini3.D0, U2.IN1
  N3: WeMos_D1_Mini3.D1, Squix1.SCL
  N4: WeMos_D1_Mini3.D2, Squix1.SCA
  N5: WeMos_D1_Mini3.D3, U3.IN1
  N6: WeMos_D1_Mini3.D4, U2.IN2
  N7: WeMos_D1_Mini3.D5, JP1.1
  N8: WeMos_D1_Mini3.D6, DS1.DQ
  N9: WeMos_D1_Mini3.D7, JP1.2
  N10: WeMos_D1_Mini3.D8, U3.IN2
  GND: WeMos_D1_Mini3.G, Squix1.GND, IC6.pin3, U2.GND, U3.GND, DS1.GND, IC7.pin2
  N11: WeMos_D1_Mini3.RST, IC6.pin4
  N12: WeMos_D1_Mini3.RX, IC7.pin1
  N13: U2.K1-In, U2.K2-In, U3.K1-In, U3.K2-In, HLK-PM1.AC#0, U4.O
  N14: U2.K2-On, M2.pin_2
  N15: JP1.3, HLK-PM1.-Vo

notes:
  Dishwasher
  Billy Cheung 2020/08/18
  Connect to 3 wires to mark
  High Water Mark
  Low Water Mark
  Bottom of Tank
  DS18B20 water temperature Sensor (Sealed in metal tube)
  Drain Pump
  220v 15Watt
  Wash Pump
  220v 80Watt
  Solenoid for inlet pipe
  220v 10Watt
  Under Water Heater
  220v 1200Watt
  220V Mains Power Supply
  Reset button
  SSD1306 OLED
  I2C
  Mains power supply
  to 5V DC 600ma
  two 2-channel or one 4-channel
  Relay module
  Low (3.3V activation)
  10A max load.
  Solenoid for drain pipe
  220v 10Watt
  Single button
  to drive the menu

custom parts:
  OLED 0.96" 128x64 I2C SSD1306 (GND/VCC): OLED 0.96" 128x64 I2C SSD1306 Pinout: GND/VCC/SCL/SDA
  DIP - 4 pins: A DIP stand-in part for whatever IC you want. With 4 pins on a 300mil dual inline package (DIP) footprint.
  2-Channel 5v Relay Shield: 2 Channel 5v Relay Shield w. 2x SPD-06VDC-SD-C
